// Logisim project Hallar_la_forma_de_dar_1.circ as structural Verilog: 1 circuit, main circuit main
module main (
  input  A,
  input  B,
  input  C,
  output out_4
);

  wire and_1_out, xor_1_out, xor_2_out;

  xor xor_1 (xor_1_out, A, B);
  xor xor_2 (xor_2_out, B, C);
  and and_1 (and_1_out, xor_1_out, xor_2_out);
  and and_2 (out_4, and_1_out, C);
endmodule
