// Logisim project Multiplicar_2_bits.circ as structural Verilog: 1 circuit, main circuit main
module main (
  input  A0,
  input  B0,
  input  A1,
  input  B1,
  output S0,
  output S1,
  output S2,
  output S3
);

  wire and_1_out, and_2_out, and_3_out, and_4_out, not_1_out, not_2_out, not_3_out, or_1_out, xor_1_out,
       xor_2_out;

  not not_1 (not_1_out, A0);
  not not_2 (not_2_out, B0);
  not not_3 (not_3_out, A1);
  xor xor_1 (xor_1_out, A0, B0);
  and and_1 (and_1_out, not_1_out, not_2_out);
  xor xor_2 (xor_2_out, B1, B0);
  or or_1 (or_1_out, xor_1_out, and_1_out);
  and and_2 (and_2_out, A0, B1, not_3_out);
  and and_3 (and_3_out, not_1_out, A1, B0);
  and and_4 (and_4_out, A0, A1, xor_2_out);
  and and_5 (S0, A0, B0);
  or or_2 (S1, and_2_out, and_3_out, and_4_out);
  and and_6 (S2, A1, B1, or_1_out);
  and and_7 (S3, A0, B0, A1, B1);
endmodule
