// Logisim project Suma_de_cuatro_bits.circ as structural Verilog: 1 circuit, main circuit main
module main (
  input  A0,
  input  A1,
  input  A2,
  input  A3,
  input  B0,
  input  B1,
  input  B2,
  input  B3,
  output C0,
  output C1,
  output C2,
  output C3,
  output C4
);

  wire and_1_out, and_2_out, and_3_out, and_4_out, and_5_out, and_6_out, and_7_out, and_8_out, and_9_out,
       and_10_out, or_1_out, or_2_out;

  and and_1 (and_1_out, B0, A0);
  and and_2 (and_2_out, A1, B1);
  and and_3 (and_3_out, B1, and_1_out);
  or or_1 (or_1_out, and_2_out, and_3_out, and_5_out);
  and and_4 (and_4_out, B2, A2);
  and and_5 (and_5_out, A1, and_1_out);
  and and_6 (and_6_out, B2, or_1_out);
  and and_7 (and_7_out, A2, or_1_out);
  or or_2 (or_2_out, and_4_out, and_6_out, and_7_out);
  and and_8 (and_8_out, or_2_out, A3);
  and and_9 (and_9_out, or_2_out, B3);
  and and_10 (and_10_out, A3, B3);
  xor xor_1 (C0, A0, B0);
  xor xor_2 (C1, and_1_out, A1, B1);
  xor xor_3 (C2, or_1_out, A2, B2);
  xor xor_4 (C3, or_2_out, A3, B3);
  or or_3 (C4, and_10_out, and_9_out, and_8_out);
endmodule
